// Logisim project Lab03.circ as structural Verilog
module Encoder (
  input  In1,
  input  In2,
  input  In3,
  input  In4,
  input  in_5,
  input  in_6,
  input  in_7,
  input  in_8,
  input  in_9
);

  // AND_Gate U1 is placed but not wired
  // AND_Gate U2 is placed but not wired
  // AND_Gate U3 is placed but not wired
  // AND_Gate U4 is placed but not wired
  // AND_Gate U5 is placed but not wired
  // AND_Gate U6 is placed but not wired
  // AND_Gate U7 is placed but not wired
  // AND_Gate U8 is placed but not wired
  // AND_Gate U9 is placed but not wired
  // AND_Gate U10 is placed but not wired
  // AND_Gate U11 is placed but not wired
  // AND_Gate U12 is placed but not wired
  // NOR_Gate U16 is placed but not wired
  // OR_Gate U13 is placed but not wired
  // OR_Gate U14 is placed but not wired
  // OR_Gate U15 is placed but not wired
  // OR_Gate U17 is placed but not wired
endmodule
