// Logisim project Lab05_Counter.circ as structural Verilog
module AsynchDownCounter (
  input  clk,
  input  rst,
  output [3:0] out_3
);

  wire d_ff_1_qn, d_ff_2_qn, d_ff_3_qn, d_ff_4_qn;

  D_Flip_Flop d_ff_1 (.D(d_ff_1_qn), .clk(clk), .Q(out_3[0]), .Qn(d_ff_1_qn), .preset(rst));  // open: reset
  D_Flip_Flop d_ff_2 (.D(d_ff_2_qn), .clk(out_3[0]), .Q(out_3[1]), .Qn(d_ff_2_qn), .preset(rst));  // open: reset
  D_Flip_Flop d_ff_3 (.D(d_ff_3_qn), .clk(out_3[1]), .Q(out_3[2]), .Qn(d_ff_3_qn), .preset(rst));  // open: reset
  D_Flip_Flop d_ff_4 (.D(d_ff_4_qn), .clk(out_3[2]), .Q(out_3[3]), .Qn(d_ff_4_qn), .preset(rst));  // open: reset
endmodule

module AsynchUpCounter (
  input  clk,
  input  rst,
  output [3:0] out_3
);

  wire d_ff_1_qn, d_ff_2_qn, d_ff_3_qn, d_ff_4_qn;

  D_Flip_Flop d_ff_1 (.D(d_ff_1_qn), .clk(clk), .Q(out_3[0]), .Qn(d_ff_1_qn), .reset(rst));  // open: preset
  D_Flip_Flop d_ff_2 (.D(d_ff_2_qn), .clk(d_ff_1_qn), .Q(out_3[1]), .Qn(d_ff_2_qn), .reset(rst));  // open: preset
  D_Flip_Flop d_ff_3 (.D(d_ff_3_qn), .clk(d_ff_2_qn), .Q(out_3[2]), .Qn(d_ff_3_qn), .reset(rst));  // open: preset
  D_Flip_Flop d_ff_4 (.D(d_ff_4_qn), .clk(d_ff_3_qn), .Q(out_3[3]), .Qn(d_ff_4_qn), .reset(rst));  // open: preset
endmodule

module AsynchDecadeCounter (
  input  clk,
  input  rst,
  output [3:0] out_3
);

  wire and_1_out, d_ff_1_qn, d_ff_2_qn, d_ff_3_qn, d_ff_4_qn, or_1_out;

  D_Flip_Flop d_ff_1 (.D(d_ff_1_qn), .clk(clk), .Q(out_3[0]), .Qn(d_ff_1_qn), .reset(or_1_out));  // open: preset
  or or_1 (or_1_out, rst, and_1_out);
  D_Flip_Flop d_ff_2 (.D(d_ff_2_qn), .clk(d_ff_1_qn), .Q(out_3[1]), .Qn(d_ff_2_qn), .reset(or_1_out));  // open: preset
  D_Flip_Flop d_ff_3 (.D(d_ff_3_qn), .clk(d_ff_2_qn), .Q(out_3[2]), .Qn(d_ff_3_qn), .reset(or_1_out));  // open: preset
  D_Flip_Flop d_ff_4 (.D(d_ff_4_qn), .clk(d_ff_3_qn), .Q(out_3[3]), .Qn(d_ff_4_qn), .reset(or_1_out));  // open: preset
  and and_1 (and_1_out, out_3[3], out_3[1]);
endmodule

module SynchRingCounter (
  input  clk,
  input  rst,
  output [3:0] out_3
);

  D_Flip_Flop d_ff_1 (.D(out_3[3]), .clk(clk), .Q(out_3[0]), .preset(rst));  // open: Qn, reset
  D_Flip_Flop d_ff_2 (.D(out_3[0]), .clk(clk), .Q(out_3[1]), .reset(rst));  // open: Qn, preset
  D_Flip_Flop d_ff_3 (.D(out_3[1]), .clk(clk), .Q(out_3[2]), .reset(rst));  // open: Qn, preset
  D_Flip_Flop d_ff_4 (.D(out_3[2]), .clk(clk), .Q(out_3[3]), .reset(rst));  // open: Qn, preset
endmodule
