// Logisim project Lab02_Bool.circ as structural Verilog: 3 circuits, main circuit main
module main (
  input  A1,
  input  B1,
  input  in_3,
  input  A2,
  input  B2,
  input  C2,
  input  D2,
  output out_8,
  output out_9
);

  Equation_1 equation_1_1 (.in_1(A1), .in_2(B1), .in_3(in_3), .Out1(out_8));
  Equation_2 equation_2_1 (.In2A(A2), .In2B(B2), .In2C(C2), .In2D(D2), .Out2(out_9));

  // Notes on the sheet:
  //   C1
  //   Ulana Zhussip
  //   Lab 2
  //   True1
  //   True2
endmodule

module Equation_2 (
  input  In2A,
  input  In2B,
  input  In2C,
  input  In2D,
  output Out2
);

  wire and_1_out, and_2_out, and_3_out, and_4_out;

  and and_1 (and_1_out, ~In2A, ~In2B, In2C, ~In2D);  // AND_Gate
  and and_2 (and_2_out, ~In2A, In2B, In2C, In2D);  // AND_Gate
  and and_3 (and_3_out, In2A, ~In2B, In2C, ~In2D);  // AND_Gate
  and and_4 (and_4_out, In2A, In2B, In2C, ~In2D);  // AND_Gate
  or or_1 (Out2, and_1_out, and_2_out, and_3_out, and_4_out);

  // Notes on the sheet:
  //   (A'B'CD')+(A'BCD)+(AB'CD')+(ABCD')
endmodule

module Equation_1 (
  input  in_1,
  input  in_2,
  input  in_3,
  output Out1
);

  wire and_1_out, and_2_out, and_3_out;

  and and_1 (and_1_out, ~in_1, in_2, ~in_3);  // AND_Gate
  and and_2 (and_2_out, in_1, ~in_2, ~in_3);  // AND_Gate
  and and_3 (and_3_out, in_1, in_3);
  or or_1 (Out1, and_1_out, and_2_out, and_3_out);

  // Notes on the sheet:
  //   (A'BC')+(AB'C')+(ABC)
endmodule
