// Logisim project Lab05_Counter.circ as structural Verilog: 7 circuits, main circuit main
module main (
  input  Reset,
  input  [2:0] sel
);

  wire clk_out;
  wire [3:0] universal_1_out_4;

  Clock #(.highDuration(4), .lowDuration(4)) clk (.out(clk_out));
  Clock sysclk ();  // open: out
  // Probe on universal_1_out_4
  Universal universal_1 (.clk(clk_out), .rst(Reset), .sel(sel), .out_4(universal_1_out_4));
  Hex_Digit_Display hex_digit_display_1 (.value(universal_1_out_4));  // open: dp
endmodule

module AsynchDownCounter (
  input  clk,
  input  rst,
  output [3:0] out_3
);

  wire d_ff_1_qn, d_ff_2_qn, d_ff_3_qn, d_ff_4_qn;

  D_Flip_Flop d_ff_1 (.D(d_ff_1_qn), .clk(clk), .Q(out_3[0]), .Qn(d_ff_1_qn), .preset(rst));  // open: reset
  D_Flip_Flop d_ff_2 (.D(d_ff_2_qn), .clk(out_3[0]), .Q(out_3[1]), .Qn(d_ff_2_qn), .preset(rst));  // open: reset
  D_Flip_Flop d_ff_3 (.D(d_ff_3_qn), .clk(out_3[1]), .Q(out_3[2]), .Qn(d_ff_3_qn), .preset(rst));  // open: reset
  D_Flip_Flop d_ff_4 (.D(d_ff_4_qn), .clk(out_3[2]), .Q(out_3[3]), .Qn(d_ff_4_qn), .preset(rst));  // open: reset
endmodule

module AsynchUpCounter (
  input  clk,
  input  rst,
  output [3:0] out_3
);

  wire d_ff_1_qn, d_ff_2_qn, d_ff_3_qn, d_ff_4_qn;

  D_Flip_Flop d_ff_1 (.D(d_ff_1_qn), .clk(clk), .Q(out_3[0]), .Qn(d_ff_1_qn), .reset(rst));  // open: preset
  D_Flip_Flop d_ff_2 (.D(d_ff_2_qn), .clk(d_ff_1_qn), .Q(out_3[1]), .Qn(d_ff_2_qn), .reset(rst));  // open: preset
  D_Flip_Flop d_ff_3 (.D(d_ff_3_qn), .clk(d_ff_2_qn), .Q(out_3[2]), .Qn(d_ff_3_qn), .reset(rst));  // open: preset
  D_Flip_Flop d_ff_4 (.D(d_ff_4_qn), .clk(d_ff_3_qn), .Q(out_3[3]), .Qn(d_ff_4_qn), .reset(rst));  // open: preset
endmodule

module AsynchDecadeCounter (
  input  clk,
  input  rst,
  output [3:0] out_3
);

  wire and_1_out, d_ff_1_qn, d_ff_2_qn, d_ff_3_qn, d_ff_4_qn, or_1_out;

  D_Flip_Flop d_ff_1 (.D(d_ff_1_qn), .clk(clk), .Q(out_3[0]), .Qn(d_ff_1_qn), .reset(or_1_out));  // open: preset
  or or_1 (or_1_out, rst, and_1_out);
  D_Flip_Flop d_ff_2 (.D(d_ff_2_qn), .clk(d_ff_1_qn), .Q(out_3[1]), .Qn(d_ff_2_qn), .reset(or_1_out));  // open: preset
  D_Flip_Flop d_ff_3 (.D(d_ff_3_qn), .clk(d_ff_2_qn), .Q(out_3[2]), .Qn(d_ff_3_qn), .reset(or_1_out));  // open: preset
  D_Flip_Flop d_ff_4 (.D(d_ff_4_qn), .clk(d_ff_3_qn), .Q(out_3[3]), .Qn(d_ff_4_qn), .reset(or_1_out));  // open: preset
  and and_1 (and_1_out, out_3[3], out_3[1]);
endmodule

module SynchRingCounter (
  input  clk,
  input  rst,
  output [3:0] out_3
);

  D_Flip_Flop d_ff_1 (.D(out_3[3]), .clk(clk), .Q(out_3[0]), .preset(rst));  // open: Qn, reset
  D_Flip_Flop d_ff_2 (.D(out_3[0]), .clk(clk), .Q(out_3[1]), .reset(rst));  // open: Qn, preset
  D_Flip_Flop d_ff_3 (.D(out_3[1]), .clk(clk), .Q(out_3[2]), .reset(rst));  // open: Qn, preset
  D_Flip_Flop d_ff_4 (.D(out_3[2]), .clk(clk), .Q(out_3[3]), .reset(rst));  // open: Qn, preset
endmodule

module JohnsonCounter (
  input  clk,
  input  rst,
  output [3:0] out_3
);

  wire d_ff_4_qn;

  D_Flip_Flop d_ff_1 (.D(d_ff_4_qn), .clk(clk), .Q(out_3[0]), .preset(rst));  // open: Qn, reset
  D_Flip_Flop d_ff_2 (.D(out_3[0]), .clk(clk), .Q(out_3[1]), .reset(rst));  // open: Qn, preset
  D_Flip_Flop d_ff_3 (.D(out_3[1]), .clk(clk), .Q(out_3[2]), .reset(rst));  // open: Qn, preset
  D_Flip_Flop d_ff_4 (.D(out_3[2]), .clk(clk), .Q(out_3[3]), .Qn(d_ff_4_qn), .reset(rst));  // open: preset
endmodule

module Universal (
  input  clk,
  input  rst,
  input  [2:0] sel,
  output [3:0] out_4
);

  wire [3:0] asynchdecadecounter_1_out_3, asynchdowncounter_1_out_3, asynchupcounter_1_out_3,
       johnsoncounter_1_out_3, synchringcounter_1_out_3;

  AsynchUpCounter asynchupcounter_1 (.clk(clk), .rst(rst), .out_3(asynchupcounter_1_out_3));
  AsynchDownCounter asynchdowncounter_1 (.clk(clk), .rst(rst), .out_3(asynchdowncounter_1_out_3));
  AsynchDecadeCounter asynchdecadecounter_1 (.clk(clk), .rst(rst), .out_3(asynchdecadecounter_1_out_3));
  SynchRingCounter synchringcounter_1 (.clk(clk), .rst(rst), .out_3(synchringcounter_1_out_3));
  JohnsonCounter johnsoncounter_1 (.clk(clk), .rst(rst), .out_3(johnsoncounter_1_out_3));
  Multiplexer #(.select(3), .width(4), .enable("false")) multiplexer_1 (
    .in0(asynchupcounter_1_out_3), .in1(asynchdowncounter_1_out_3), .in2(asynchdecadecounter_1_out_3),
    .in3(synchringcounter_1_out_3), .in4(johnsoncounter_1_out_3), .out(out_4), .sel(sel));  // open: in5, in6, in7
endmodule
